// Logisim project control-logic.circ as structural Verilog: 1 circuit, main circuit control_logic
module control_logic (
  input  [31:0] inst,
  input  BrEq,
  input  BrLt,
  output PCSel,
  output RegWEn,
  output [2:0] ImmSel,
  output BrUn,
  output ASel,
  output BSel,
  output [3:0] ALUSel,
  output MemRW,
  output [1:0] WBSel,
  output CSRSel,
  output CSRWen
);

  wire add0, addi0, and7, comparator_3_eq, comparator_10_eq, comparator_11_eq, comparator_12_eq,
       comparator_13_eq, comparator_14_eq, comparator_15_eq, comparator_16_eq, comparator_17_eq,
       comparator_18_eq, I_Type, mul8, mulh9, mulhu11, or6, R_Type, sll1, slli1, slt2, sra13, srl5, sub12,
       xor4;
  wire [3:0] I_ALUSel, priority_encoder_1_out, R_ALUSel;

  Demultiplexer #(.enable("false"), .select(2)) demultiplexer_1 (
    .out0(add0), .out1(mul8), .out2(sub12), .in(addi0), .sel({inst[30], inst[25]}));  // open: out3
  Comparator #(.mode("unsigned"), .width(3)) comparator_1 (.a(inst[14:12]), .b(3'b000), .eq(addi0));  // open: gt, lt
  Demultiplexer #(.enable("false")) demultiplexer_2 (.out0(sll1), .out1(mulh9), .in(slli1), .sel(inst[25]));
  Comparator #(.mode("unsigned"), .width(3)) comparator_2 (.a(inst[14:12]), .b(3'b001), .eq(slli1));  // open: gt, lt
  Demultiplexer #(.enable("false")) demultiplexer_3 (.out0(srl5), .out1(sra13), .in(comparator_3_eq), .sel(inst[30]));
  Comparator #(.mode("unsigned"), .width(3)) comparator_3 (
    .a(inst[14:12]), .b(3'b101), .eq(comparator_3_eq));  // open: gt, lt
  Comparator #(.mode("unsigned"), .width(3)) comparator_4 (.a(inst[14:12]), .b(3'b011), .eq(mulhu11));  // open: gt, lt
  Comparator #(.mode("unsigned"), .width(3)) comparator_5 (.a(inst[14:12]), .b(3'b010), .eq(slt2));  // open: gt, lt
  Comparator #(.mode("unsigned"), .width(3)) comparator_6 (.a(inst[14:12]), .b(3'b100), .eq(xor4));  // open: gt, lt
  Comparator #(.mode("unsigned"), .width(3)) comparator_7 (.a(inst[14:12]), .b(3'b110), .eq(or6));  // open: gt, lt
  Comparator #(.mode("unsigned"), .width(3)) comparator_8 (.a(inst[14:12]), .b(3'b111), .eq(and7));  // open: gt, lt
  Comparator #(.mode("unsigned"), .width(7)) comparator_9 (.a(inst[6:0]), .b(7'b0110011), .eq(R_Type));  // open: gt, lt
  Comparator #(.mode("unsigned"), .width(7)) comparator_10 (
    .a(inst[6:0]), .b(7'b0000011), .eq(comparator_10_eq));  // open: gt, lt
  Comparator #(.mode("unsigned"), .width(7)) comparator_11 (
    .a(inst[6:0]), .b(7'b0010011), .eq(comparator_11_eq));  // open: gt, lt
  Comparator #(.mode("unsigned"), .width(7)) comparator_12 (
    .a(inst[6:0]), .b(7'b0110011), .eq(comparator_12_eq));  // open: gt, lt
  Comparator #(.mode("unsigned"), .width(7)) comparator_13 (
    .a(inst[6:0]), .b(7'b0000011), .eq(comparator_13_eq));  // open: gt, lt
  Comparator #(.mode("unsigned"), .width(7)) comparator_14 (
    .a(inst[6:0]), .b(7'b0010011), .eq(comparator_14_eq));  // open: gt, lt
  Comparator #(.mode("unsigned"), .width(7)) comparator_15 (
    .a(inst[6:0]), .b(7'b0010111), .eq(comparator_15_eq));  // open: gt, lt
  Comparator #(.mode("unsigned"), .width(7)) comparator_16 (
    .a(inst[6:0]), .b(7'b0110111), .eq(comparator_16_eq));  // open: gt, lt
  Comparator #(.mode("unsigned"), .width(7)) comparator_17 (
    .a(inst[6:0]), .b(7'b1101111), .eq(comparator_17_eq));  // open: gt, lt
  Comparator #(.mode("unsigned"), .width(7)) comparator_18 (
    .a(inst[6:0]), .b(7'b1100111), .eq(comparator_18_eq));  // open: gt, lt
  or or_1 (I_Type, comparator_10_eq, comparator_11_eq);
  or or_2 (RegWEn, comparator_12_eq, comparator_13_eq, comparator_14_eq, comparator_15_eq, comparator_16_eq, comparator_17_eq, comparator_18_eq);
  Multiplexer #(.enable("false"), .select(2), .width(4)) multiplexer_1 (
    .in0(4'b0000), .in1(R_ALUSel), .in2(I_ALUSel), .out(ALUSel), .sel({I_Type, R_Type}));  // open: in3
  Priority_Encoder #(.select(4)) priority_encoder_1 (
    .in0(addi0), .in1(slli1), .in2(slt2), .in4(xor4), .in5(srl5), .in6(or6), .in7(and7), .in13(sra13),
    .out(priority_encoder_1_out));  // open: in3, in8, in9, in10, in11, in12, in14, in15, gs, en_out, en_in
  Priority_Encoder #(.select(4)) priority_encoder_2 (
    .in0(add0), .in1(sll1), .in2(slt2), .in4(xor4), .in5(srl5), .in6(or6), .in7(and7), .in8(mul8),
    .in9(mulh9), .in11(mulhu11), .in12(sub12), .in13(sra13), .out(R_ALUSel));  // open: in3, in10, in14, in15, gs, en_out, en_in
  Multiplexer #(.enable("false"), .width(4)) multiplexer_2 (
    .in0(4'b0000), .in1(priority_encoder_1_out), .out(I_ALUSel), .sel(inst[4]));
  Comparator #(.mode("unsigned"), .width(7)) comparator_19 (
    .a(inst[6:0]), .b(7'b1110011), .eq(CSRWen));  // open: gt, lt
  Comparator #(.mode("unsigned"), .width(7)) comparator_20 (.a(inst[6:0]), .b(7'b0100011), .eq(MemRW));  // open: gt, lt
  Comparator #(.mode("unsigned"), .width(7)) comparator_21 (.a(inst[6:0]), .b(7'b0110011), .eq(BSel));  // open: gt, lt
  Comparator #(.mode("unsigned"), .width(7)) comparator_22 (.a(inst[6:0]), .b(7'b0010111), .eq(ASel));  // open: gt, lt

  assign BrUn = inst[13];

  // Other names for the same wires on the sheet: opcode[6:0] = inst[6:0]; is_arithmetic = inst[4];
  //   funct3[2:0] = inst[14:12]; bit25 = inst[25]; funct7[6:0] = inst[31:25]; bit30 = inst[30]

  // Notes on the sheet:
  //   R-Type
  //   I-Type (loads)
  //   I-Type (arithmetic)
  //   auipc
  //   lui
  //   jal
  //   jalr
  //   INPUTS to your circuit
  //   DON'T CHANGE THE LOCATIONS OF THE INPUTS AND OUTPUTS!
  //   OUTPUT from your circuit
endmodule
